# Fritzing sketch ProMiniISP (saved by Fritzing 0.9.3b)
breadboards: 1

parts:
  Part1 = Arduino Pro Mini v13  # not connected
  Part2 = Arduino Pro Mini v13
  Part3 = Adafruit FTDI Friend [part_number="Adafruit #284"]

nets:
  N1: Part2.DTR, Part3.RTS/DTR
  N2: Part2.D0/TX, Part3.RX
  N3: Part2.D1/RX, Part3.TX
  VCC: Part2.VCC, Part3.VCC
  GND: Part2.GND, Part3.GND, Part3.CTS

notes:
  FTDI / CH340
  Serial adapter
  First Pro Mini
  Acting as ISP
  Second Pro Mini
  Being programmed

custom parts:
  Adafruit FTDI Friend: Long gone are the days of parallel ports and serial ports. Now the USB port reigns supreme! But USB is hard, and you just want to transfer your every-day serial data from a microcontroller to computer. What now? Enter the FTDI Friend! The FTDI Friend is a tweaked out FTDI FT232RL chip adapter. Sure, like the well-known FTDI cable, it can provide power to your project and there are 4 signal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
